# Fritzing sketch Gepresa (saved by Fritzing 0.9.3b)
breadboards: 1

parts:
  NodeMCU_ESP8266_Lolin = RFID-RC522-v2
  U1 = ESP8266 NodeMCU LoLin module
  LED1 = smd LED [color="Red (635nm)" package="0603 [SMD]"]
  LED2 = smd LED [color="Orange (605nm)" package="0603 [SMD]"]
  LED3 = smd LED [color="Green (570nm)" package="0603 [SMD]"]

nets:
  N1: NodeMCU_ESP8266_Lolin.SDA, U1.D4
  N2: NodeMCU_ESP8266_Lolin.SCK, U1.D5
  N3: NodeMCU_ESP8266_Lolin.MOSI, U1.D7
  N4: NodeMCU_ESP8266_Lolin.MISO, U1.D6
  GND: NodeMCU_ESP8266_Lolin.GND, U1.GND, LED1.cathode, LED2.cathode, LED3.cathode
  N5: NodeMCU_ESP8266_Lolin.RST, U1.D2
  3.3V: NodeMCU_ESP8266_Lolin.3.3V, U1.3V3
  N6: U1.D0, LED1.anode
  N7: U1.D1, LED3.anode
  N8: U1.D8, LED2.anode

custom parts:
  RFID-RC522-v2: A simple China made RFID-RC522 Reader; do check the pin labels, as this is a MFRC522 based clone.
  ESP8266 NodeMCU LoLin module: ESP8266 based NodeMCU
